# Fritzing sketch scheme (saved by Fritzing 0.9.6b)
breadboards: 1

parts:
  MH-ET_LIVE_ESP32_DEVKIT1 = MH-ET LIVE ESP32 DEVKIT 38 pins
  Componente1 = GY-VL53L0XV2 Laser Ranger Module
  DHT1 = DHT22 Humidity and Temperature Sensor
  R1 = Resistor [tolerance=±5% resistance=10k package="2512 [SMD]"]
  M1 = DC Motor [voltage_(max)=6V voltage_(min)=3V]
  S1 = H-Bridge with L298N
  Part1 = Adafruit USB Type C Breakout [part_number=4090]
  Buck_Convertor1 = Buck Convertor [part_number=LM2596 package=THT]

nets:
  3V3: MH-ET_LIVE_ESP32_DEVKIT1.3V3, Componente1.VCC, DHT1.VDD, R1.Pin_0
  N1: MH-ET_LIVE_ESP32_DEVKIT1.GND#58, Buck_Convertor1.Negative_Output
  5V: MH-ET_LIVE_ESP32_DEVKIT1.5V, S1.5V, Buck_Convertor1.Positive_Output
  GND: MH-ET_LIVE_ESP32_DEVKIT1.GND#64, Componente1.GND, DHT1.GND, S1.GND
  N2: MH-ET_LIVE_ESP32_DEVKIT1.IO22, Componente1.SCL
  N3: MH-ET_LIVE_ESP32_DEVKIT1.IO21, Componente1.SDA
  N4: MH-ET_LIVE_ESP32_DEVKIT1.IO17, S1.IN2
  N5: MH-ET_LIVE_ESP32_DEVKIT1.IO16, S1.IN1
  N6: MH-ET_LIVE_ESP32_DEVKIT1.IO4, DHT1.DATA, R1.Pin_1
  N7: M1.pin_1, S1.M1-02
  N8: M1.pin_2, S1.M1-01
  N9: S1.12V, Part1.VBUS, Buck_Convertor1.Positive_Input
  N10: S1.ENA, S1.ENA-5V
  N11: S1.ENB, S1.ENB-5V
  N12: Part1.GND, Buck_Convertor1.Negative_Input

notes:
  PUMP
  TEMPERATURE/HUMIDITY SENSOR
  LEVEL SENSOR
  TOUCH SENSOR
  MOTOR DRIVER
  DC-DC STEP DOWN
  USB-C PD TRIGGER BOARD

custom parts:
  MH-ET LIVE ESP32 DEVKIT 38 pins: http://mh.nodebb.com/topic/2/mh-et-live-esp32-devkit
  GY-VL53L0XV2 Laser Ranger Module: The GY-VL53L0XV2 is based on the VL53L0X from ST Microelectronics, a time-of-flight ranging system integrated into a compact module.
  H-Bridge with L298N: h-bridge
  Adafruit USB Type C Breakout: Adafruit breakout board for USB Type C socket.
  Buck Convertor: DC to DC buck convertor
